# Fritzing sketch circuit (saved by Fritzing 0.9.3b)
breadboards: 1

parts:
  DHT11 = Humidity and Temperature Sensor DHT11
  Part1 = LCD1602-I2C
  U1 = NodeMCU V1.0
  Part2 = HC-SR501 Body Sensor Module  # not connected

nets (from the schematic view):
  VCC: DHT11.Vcc, Part1.VCC, U1.Vin
  N1: DHT11.Data-signal, U1.D5
  GND: DHT11.GND_2, Part1.GND, U1.GND
  N2: Part1.SDA, U1.D2
  N3: Part1.SCL, U1.D1

custom parts:
  Humidity and Temperature Sensor DHT11: Digital relative humidity & temperature sensor DHT11
  LCD1602-I2C: A standard character display, usually with 2x16 characters. Comes in many colors with LCM1602 IIC attached.
  NodeMCU V1.0: ESP8266 based NodeMCU
  HC-SR501 Body Sensor Module: Pyroelectric Infrared PIR Motion Sensor Detector Module
